# Fritzing sketch circuit_diagram (saved by Fritzing 1.0.3b)

parts:
  Mod1 = Raspberry Pi 4B
  Part1 = Arduino Nano (Rev3.0)
  S2 = Round Pushbutton
  Digital_Panel_Meter_Voltage_DMS-20PC_by_Murata1 = Digital Panel Meter, Voltage, DMS-20PC
  A1 = mini boost module
  F1 = FUSE [package=fuse_5mm]
  M1 = RPlidar A1M8 [package=THT]
  J1 = Wago 221-415
  J2 = Wago 221-415
  L298N2 = L298N DC motor driver
  USBTTL1 = USB A Plug
  USBTTL2 = Micro USB B Plug
  J3 = Wago 221-415
  J4 = Wago 221-415
  USBTTL4 = Micro USB B Plug
  DC_Mot_Enc1 = DC Motor with two-phase hall-encoder [part_number=VT-E-G25A-06-177E]
  DC_Mot_Enc2 = DC Motor with two-phase hall-encoder [part_number=VT-E-G25A-06-177E]
  IC2 = Rasberry Pi NIOR Camera [chip_label=IC package="DIP (Dual Inline) [THT]"]  # not connected
  BAT2 = 18650 battery holder [package=battery-18650-kit]
  BAT3 = 18650 battery holder [package=battery-18650-kit]
  BAT4 = 18650 battery holder [package=battery-18650-kit]

nets:
  N1: Mod1.GND, M1.pin3
  N2: Mod1.GPIO14, M1.pin1
  N3: Mod1.GPIO15, M1.pin2
  N4: Part1.GND, DC_Mot_Enc1.pin2, DC_Mot_Enc2.pin2
  N5: Part1.D2, DC_Mot_Enc2.pin3
  N6: Part1.D3, DC_Mot_Enc2.pin4
  N7: Part1.D5, L298N2.IN4
  N8: Part1.D6, L298N2.IN1
  N9: Part1.D9, L298N2.IN3
  N10: Part1.D10, L298N2.IN2
  N11: Part1.D12/MISO, L298N2.ENB
  N12: Part1.5V, DC_Mot_Enc1.pin5, DC_Mot_Enc2.pin5
  N13: Part1.A5, DC_Mot_Enc1.pin4
  N14: Part1.A4, DC_Mot_Enc1.pin3
  N15: Part1.D13/SCK, L298N2.ENA
  N16: S2.leg0, F1.2
  N17: S2.leg1, Digital_Panel_Meter_Voltage_DMS-20PC_by_Murata1.1:_VCC, A1.Pin_2, J1.Pin_1, J1.Pin_2, J1.Pin_3, J1.Pin_4, J1.Pin_5, L298N2.12V
  N18: Digital_Panel_Meter_Voltage_DMS-20PC_by_Murata1.6:_#DP1, A1.Pin_1, J2.Pin_1, J2.Pin_2, J2.Pin_3, J2.Pin_4, J2.Pin_5, L298N2.GND, BAT4.-
  N19: A1.Pin_3, A1.Pin_4, M1.pin4, M1.pin5, M1.pin7, L298N2.5V, J3.Pin_1, J3.Pin_3, J3.Pin_4, J3.Pin_5, J4.Pin_1, J4.Pin_2, J4.Pin_3, J4.Pin_4, J4.Pin_5, USBTTL4.usb
  N20: F1.1, BAT2.+
  N21: L298N2.OUT1, DC_Mot_Enc2.pin6
  N22: L298N2.OUT2, DC_Mot_Enc2.pin1
  N23: L298N2.OUT3, DC_Mot_Enc1.pin6
  N24: L298N2.OUT4, DC_Mot_Enc1.pin1
  N25: USBTTL1.usb, USBTTL2.usb
  N26: BAT2.-, BAT3.+
  N27: BAT3.-, BAT4.+

notes:
  Raspberry PI
  LIDAR
  Distribución 12 V
  L298N
  Batería 12V
  Distribución 5 V
  Multímetro
  Regulador de tensión
  Fusible
  Interruptor
  Arduino Nano
  Motor DC con encoder (derecho)
  Motor DC con encoder (izquierdo)

custom parts:
  mini boost module: mini boost module.
  RPlidar A1M8: .The RPLIDAR A1 is the next generation low cost 360 degree 2D laser scanner (LIDAR) solution developed by SLAMTEC. It can take up to 4000 samples of laser ranging per second with high rotation speed. And equipped with SLAMTEC patented OPTMAG technology, it breakouts the life limitation of traditional LIDAR system so as to work stably for a long time.
  Wago 221-415: Wago 221-415 5 position splicing connector 12AWG.
  L298N DC motor driver: 2x DC motor driver with 78M05 positive voltage regulator (7..35 V) L298N: max 46 V, 2 A Set 5 V Enable jumper to enable 5 V regultor (needed for the L298N) and +5 V output at screw terminal or supply external +5 V at screw terminal Set ENA and/or ENB to +5 V to enable motor permanently or supply ENA and/or ENB with PWM signal IN1 and IN2 set rotation directory for motor A (OUT1/OUT2) IN2 and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
  Rasberry Pi NIOR Camera: Camera
  18650 battery holder: 18650 Battery Holder
